// Logisim project display.circ as structural Verilog
module Display_Driver (
  input  [7:0] data,
  input  [3:0] pos,
  input  [3:0] addr,
  input  clk,
  input  dir,
  output [3:0] out_6,
  output [3:0] out_7,
  output [7:0] data_2,
  output [3:0] pos_2,
  output [3:0] addr_2,
  output clk_2,
  output dir_2,
  output [3:0] pos_3
);

  wire and_1_out, and_2_out, comparator_1_eq, not_1_out;
  wire [7:0] register_1_q;

  Comparator #(.width(4)) comparator_1 (.a(addr), .b(pos), .eq(comparator_1_eq));  // open: gt, lt
  and and_1 (and_1_out, comparator_1_eq, dir);
  Register register_1 (.D(data), .en(and_1_out), .Q(register_1_q), .clk(clk));  // open: clr
  // Probe on register_1_q
  assign data_2 = and_2_out ? register_1_q : 8'bz;  // Controlled_Buffer controlled_buffer_1
  and and_2 (and_2_out, ~dir, comparator_1_eq);  // AND_Gate
  not not_1 (not_1_out, and_2_out);
  assign data_2 = not_1_out ? data : 8'bz;  // Controlled_Buffer controlled_buffer_2
  Adder #(.width(4)) adder_1 (.a(pos), .b(4'b0001), .out(pos_2));  // open: cin, cout

  assign addr_2 = addr;
  assign clk_2 = clk;
  assign dir_2 = dir;
  assign pos_3 = pos;

  // Notes on the sheet:
  //   Add bcd here
endmodule
