// Logisim project main.circ as structural Verilog: 5 circuits, main circuit main
module main (
);

  wire button_1_out, button_2_trigger, button_3_out, button_6_out, button_8_out, button_10_out,
       button_12_out, clock_1_out, display_driver_2_clk_2, display_driver_2_dir_2, display_driver_2_isempty,
       display_driver_3_clk_2, display_driver_3_dir_2, display_driver_4_clk_2, display_driver_4_dir_2,
       display_driver_5_clk_2, display_driver_5_dir_2, display_driver_6_clk_2, display_driver_6_dir_2,
       display_driver_7_clk_2, display_driver_7_dir_2, display_driver_8_clk_2, display_driver_8_dir_2,
       display_driver_9_clk_2, display_driver_9_dir_2, display_driver_10_clk_2, display_driver_10_dir_2,
       display_driver_11_clk_2, display_driver_11_dir_2, display_driver_12_clk_2, display_driver_12_dir_2,
       display_driver_13_clk_2, display_driver_13_dir_2, display_driver_14_clk_2, display_driver_14_dir_2,
       pull_resistor_1_node;
  wire [3:0] button_2_addr_2, button_4_addr_2, button_5_addr_2, button_7_addr_2, button_9_addr_2,
       button_11_addr_2, display_driver_1_out_6, display_driver_1_out_7, display_driver_2_addr_2,
       display_driver_2_out_6, display_driver_2_out_7, display_driver_2_pos_2, display_driver_3_addr_2,
       display_driver_3_out_6, display_driver_3_out_7, display_driver_3_pos_2, display_driver_3_pos_3,
       display_driver_4_addr_2, display_driver_4_out_6, display_driver_4_out_7, display_driver_4_pos_2,
       display_driver_5_addr_2, display_driver_5_out_6, display_driver_5_out_7, display_driver_5_pos_2,
       display_driver_5_pos_3, display_driver_6_addr_2, display_driver_6_out_6, display_driver_6_out_7,
       display_driver_6_pos_2, display_driver_7_addr_2, display_driver_7_out_6, display_driver_7_out_7,
       display_driver_7_pos_2, display_driver_7_pos_3, display_driver_8_addr_2, display_driver_8_out_6,
       display_driver_8_out_7, display_driver_8_pos_2, display_driver_9_addr_2, display_driver_9_out_6,
       display_driver_9_out_7, display_driver_9_pos_2, display_driver_9_pos_3, display_driver_10_addr_2,
       display_driver_10_out_6, display_driver_10_out_7, display_driver_10_pos_2, display_driver_11_addr_2,
       display_driver_11_out_6, display_driver_11_out_7, display_driver_11_pos_2, display_driver_11_pos_3,
       display_driver_12_addr_2, display_driver_12_out_6, display_driver_12_out_7, display_driver_12_pos_2,
       display_driver_13_addr_2, display_driver_13_out_6, display_driver_13_out_7, display_driver_13_pos_2,
       display_driver_13_pos_3, display_driver_14_addr_2, display_driver_14_out_6, display_driver_14_out_7,
       inc4_1_out, pos, undriven;
  wire [7:0] adder_2_out, adder_3_out, adder_4_out, adder_5_out, adder_6_out, adder_7_out, adder_8_out,
       adder_9_out, adder_10_out, adder_11_out, adder_12_out, adder_13_out, adder_14_out, botScore,
       display_driver_1_register, display_driver_2_data_2, display_driver_2_register,
       display_driver_3_data_2, display_driver_3_register, display_driver_4_data_2,
       display_driver_4_register, display_driver_5_data_2, display_driver_5_register,
       display_driver_6_data_2, display_driver_6_register, display_driver_7_data_2,
       display_driver_7_register, display_driver_8_data_2, display_driver_8_register,
       display_driver_9_data_2, display_driver_9_register, display_driver_10_data_2,
       display_driver_10_register, display_driver_11_data_2, display_driver_11_register,
       display_driver_12_data_2, display_driver_12_register, display_driver_13_data_2,
       display_driver_13_register, display_driver_14_data_2, display_driver_14_register, I_Odat_in;

  Display_Driver display_driver_1 (
    .data(display_driver_2_data_2), .pos(display_driver_2_pos_2), .addr(display_driver_2_addr_2),
    .clk(display_driver_2_clk_2), .dir(display_driver_2_dir_2), .out_6(display_driver_1_out_6),
    .out_7(display_driver_1_out_7), .register(display_driver_1_register), .data_2(I_Odat_in));  // open: pos_2, addr_2, clk_2, dir_2, pos_3, isEmpty
  adder adder_1 (.in1(adder_2_out), .in2(display_driver_1_register), .out(botScore));
  Hex_Digit_Display hex_digit_display_1 (.value(display_driver_1_out_6), .dp(1'b0));
  Hex_Digit_Display hex_digit_display_2 (.value(display_driver_1_out_7), .dp(1'b0));
  Clock clock_1 (.out(clock_1_out));
  // Probe on button_2_addr_2
  Display_Driver display_driver_2 (
    .data(display_driver_4_data_2), .pos(display_driver_4_pos_2), .addr(display_driver_4_addr_2),
    .clk(display_driver_4_clk_2), .dir(display_driver_4_dir_2), .out_6(display_driver_2_out_6),
    .out_7(display_driver_2_out_7), .register(display_driver_2_register), .data_2(display_driver_2_data_2),
    .pos_2(display_driver_2_pos_2), .addr_2(display_driver_2_addr_2), .clk_2(display_driver_2_clk_2),
    .dir_2(display_driver_2_dir_2), .isEmpty(display_driver_2_isempty));  // open: pos_3
  adder adder_2 (.in1(adder_5_out), .in2(display_driver_2_register), .out(adder_2_out));
  Hex_Digit_Display hex_digit_display_3 (.value(display_driver_2_out_6), .dp(1'b0));
  Hex_Digit_Display hex_digit_display_4 (.value(display_driver_2_out_7), .dp(1'b0));
  Hex_Digit_Display hex_digit_display_5 (.value(display_driver_3_out_6), .dp(1'b0));
  Hex_Digit_Display hex_digit_display_6 (.value(display_driver_3_out_7), .dp(1'b0));
  Pull_Resistor pull_resistor_1 (.node(pull_resistor_1_node));
  adder adder_3 (.in1({8{1'b0}}), .in2(display_driver_3_register), .out(adder_3_out));
  Display_Driver display_driver_3 (
    .data({8{1'b0}}), .pos(4'b0001), .addr(4'b0000), .clk(clock_1_out), .dir(1'b0),
    .out_6(display_driver_3_out_6), .out_7(display_driver_3_out_7), .register(display_driver_3_register),
    .data_2(display_driver_3_data_2), .pos_2(display_driver_3_pos_2), .addr_2(display_driver_3_addr_2),
    .clk_2(display_driver_3_clk_2), .dir_2(display_driver_3_dir_2), .pos_3(display_driver_3_pos_3),
    .isEmpty(pull_resistor_1_node));
  Button button_1 (.out(button_1_out));
  Display_Driver display_driver_4 (
    .data(display_driver_6_data_2), .pos(display_driver_6_pos_2), .addr(display_driver_6_addr_2),
    .clk(display_driver_6_clk_2), .dir(display_driver_6_dir_2), .out_6(display_driver_4_out_6),
    .out_7(display_driver_4_out_7), .register(display_driver_4_register), .data_2(display_driver_4_data_2),
    .pos_2(display_driver_4_pos_2), .addr_2(display_driver_4_addr_2), .clk_2(display_driver_4_clk_2),
    .dir_2(display_driver_4_dir_2), .isEmpty(display_driver_2_isempty));  // open: pos_3
  Hex_Digit_Display hex_digit_display_7 (.value(display_driver_4_out_6), .dp(1'b0));
  Hex_Digit_Display hex_digit_display_8 (.value(display_driver_5_out_6), .dp(1'b0));
  adder adder_4 (.in1(adder_3_out), .in2(display_driver_5_register), .out(adder_4_out));
  Display_Driver display_driver_5 (
    .data(display_driver_3_data_2), .pos(display_driver_3_pos_2), .addr(display_driver_3_addr_2),
    .clk(display_driver_3_clk_2), .dir(display_driver_3_dir_2), .out_6(display_driver_5_out_6),
    .out_7(display_driver_5_out_7), .register(display_driver_5_register), .data_2(display_driver_5_data_2),
    .pos_2(display_driver_5_pos_2), .addr_2(display_driver_5_addr_2), .clk_2(display_driver_5_clk_2),
    .dir_2(display_driver_5_dir_2), .pos_3(display_driver_5_pos_3), .isEmpty(pull_resistor_1_node));
  button button_2 (
    .addr_2(button_2_addr_2), .addr(button_4_addr_2), .pos(display_driver_3_pos_3), .button(button_1_out),
    .trigger(button_2_trigger));
  Button button_3 (.out(button_3_out));
  adder adder_5 (.in1(adder_7_out), .in2(display_driver_4_register), .out(adder_5_out));
  Hex_Digit_Display hex_digit_display_9 (.value(display_driver_6_out_6), .dp(1'b0));
  Hex_Digit_Display hex_digit_display_10 (.value(display_driver_4_out_7), .dp(1'b0));
  Hex_Digit_Display hex_digit_display_11 (.value(display_driver_5_out_7), .dp(1'b0));
  Hex_Digit_Display hex_digit_display_12 (.value(display_driver_7_out_6), .dp(1'b0));
  adder adder_6 (.in1(adder_4_out), .in2(display_driver_7_register), .out(adder_6_out));
  button button_4 (
    .addr_2(button_4_addr_2), .addr(button_5_addr_2), .pos(display_driver_5_pos_3), .button(button_3_out),
    .trigger(button_2_trigger));
  Display_Driver display_driver_6 (
    .data(display_driver_8_data_2), .pos(display_driver_8_pos_2), .addr(display_driver_8_addr_2),
    .clk(display_driver_8_clk_2), .dir(display_driver_8_dir_2), .out_6(display_driver_6_out_6),
    .out_7(display_driver_6_out_7), .register(display_driver_6_register), .data_2(display_driver_6_data_2),
    .pos_2(display_driver_6_pos_2), .addr_2(display_driver_6_addr_2), .clk_2(display_driver_6_clk_2),
    .dir_2(display_driver_6_dir_2), .isEmpty(display_driver_2_isempty));  // open: pos_3
  adder adder_7 (.in1(adder_8_out), .in2(display_driver_6_register), .out(adder_7_out));
  Hex_Digit_Display hex_digit_display_13 (.value(display_driver_8_out_6), .dp(1'b0));
  Hex_Digit_Display hex_digit_display_14 (.value(display_driver_6_out_7), .dp(1'b0));
  Hex_Digit_Display hex_digit_display_15 (.value(display_driver_7_out_7), .dp(1'b0));
  Hex_Digit_Display hex_digit_display_16 (.value(display_driver_9_out_6), .dp(1'b0));
  Display_Driver display_driver_7 (
    .data(display_driver_5_data_2), .pos(display_driver_5_pos_2), .addr(display_driver_5_addr_2),
    .clk(display_driver_5_clk_2), .dir(display_driver_5_dir_2), .out_6(display_driver_7_out_6),
    .out_7(display_driver_7_out_7), .register(display_driver_7_register), .data_2(display_driver_7_data_2),
    .pos_2(display_driver_7_pos_2), .addr_2(display_driver_7_addr_2), .clk_2(display_driver_7_clk_2),
    .dir_2(display_driver_7_dir_2), .pos_3(display_driver_7_pos_3), .isEmpty(pull_resistor_1_node));
  button button_5 (
    .addr_2(button_5_addr_2), .addr(button_7_addr_2), .pos(display_driver_7_pos_3), .button(button_6_out),
    .trigger(button_2_trigger));
  Button button_6 (.out(button_6_out));
  Display_Driver display_driver_8 (
    .data(display_driver_10_data_2), .pos(display_driver_10_pos_2), .addr(display_driver_10_addr_2),
    .clk(display_driver_10_clk_2), .dir(display_driver_10_dir_2), .out_6(display_driver_8_out_6),
    .out_7(display_driver_8_out_7), .register(display_driver_8_register), .data_2(display_driver_8_data_2),
    .pos_2(display_driver_8_pos_2), .addr_2(display_driver_8_addr_2), .clk_2(display_driver_8_clk_2),
    .dir_2(display_driver_8_dir_2), .isEmpty(display_driver_2_isempty));  // open: pos_3
  adder adder_8 (.in1(adder_10_out), .in2(display_driver_8_register), .out(adder_8_out));
  Hex_Digit_Display hex_digit_display_17 (.value(display_driver_10_out_6), .dp(1'b0));
  Hex_Digit_Display hex_digit_display_18 (.value(display_driver_8_out_7), .dp(1'b0));
  Hex_Digit_Display hex_digit_display_19 (.value(display_driver_11_out_6), .dp(1'b0));
  Hex_Digit_Display hex_digit_display_20 (.value(display_driver_9_out_7), .dp(1'b0));
  adder adder_9 (.in1(adder_6_out), .in2(display_driver_9_register), .out(adder_9_out));
  Display_Driver display_driver_9 (
    .data(display_driver_7_data_2), .pos(display_driver_7_pos_2), .addr(display_driver_7_addr_2),
    .clk(display_driver_7_clk_2), .dir(display_driver_7_dir_2), .out_6(display_driver_9_out_6),
    .out_7(display_driver_9_out_7), .register(display_driver_9_register), .data_2(display_driver_9_data_2),
    .pos_2(display_driver_9_pos_2), .addr_2(display_driver_9_addr_2), .clk_2(display_driver_9_clk_2),
    .dir_2(display_driver_9_dir_2), .pos_3(display_driver_9_pos_3), .isEmpty(pull_resistor_1_node));
  button button_7 (
    .addr_2(button_7_addr_2), .addr(button_9_addr_2), .pos(display_driver_9_pos_3), .button(button_8_out),
    .trigger(button_2_trigger));
  Button button_8 (.out(button_8_out));
  Display_Driver display_driver_10 (
    .data(display_driver_12_data_2), .pos(display_driver_12_pos_2), .addr(display_driver_12_addr_2),
    .clk(display_driver_12_clk_2), .dir(display_driver_12_dir_2), .out_6(display_driver_10_out_6),
    .out_7(display_driver_10_out_7), .register(display_driver_10_register),
    .data_2(display_driver_10_data_2), .pos_2(display_driver_10_pos_2), .addr_2(display_driver_10_addr_2),
    .clk_2(display_driver_10_clk_2), .dir_2(display_driver_10_dir_2), .isEmpty(display_driver_2_isempty));  // open: pos_3
  adder adder_10 (.in1(adder_12_out), .in2(display_driver_10_register), .out(adder_10_out));
  Hex_Digit_Display hex_digit_display_21 (.value(undriven), .dp(1'b0));
  Hex_Digit_Display hex_digit_display_22 (.value(display_driver_11_out_7), .dp(1'b0));
  adder adder_11 (.in1(adder_9_out), .in2(display_driver_11_register), .out(adder_11_out));
  Display_Driver display_driver_11 (
    .data(display_driver_9_data_2), .pos(display_driver_9_pos_2), .addr(display_driver_9_addr_2),
    .clk(display_driver_9_clk_2), .dir(display_driver_9_dir_2), .out_6(display_driver_11_out_6),
    .out_7(display_driver_11_out_7), .register(display_driver_11_register),
    .data_2(display_driver_11_data_2), .pos_2(display_driver_11_pos_2), .addr_2(display_driver_11_addr_2),
    .clk_2(display_driver_11_clk_2), .dir_2(display_driver_11_dir_2), .pos_3(display_driver_11_pos_3),
    .isEmpty(pull_resistor_1_node));
  button button_9 (
    .addr_2(button_9_addr_2), .addr(button_11_addr_2), .pos(display_driver_11_pos_3), .button(button_10_out),
    .trigger(button_2_trigger));
  Button button_10 (.out(button_10_out));
  Display_Driver display_driver_12 (
    .data(display_driver_14_data_2), .pos(inc4_1_out), .addr(display_driver_14_addr_2),
    .clk(display_driver_14_clk_2), .dir(display_driver_14_dir_2), .out_6(display_driver_12_out_6),
    .out_7(display_driver_12_out_7), .register(display_driver_12_register),
    .data_2(display_driver_12_data_2), .pos_2(display_driver_12_pos_2), .addr_2(display_driver_12_addr_2),
    .clk_2(display_driver_12_clk_2), .dir_2(display_driver_12_dir_2), .isEmpty(display_driver_2_isempty));  // open: pos_3
  adder adder_12 (.in1({8{1'b0}}), .in2(display_driver_12_register), .out(adder_12_out));
  Hex_Digit_Display hex_digit_display_23 (.value(display_driver_12_out_6), .dp(1'b0));
  Hex_Digit_Display hex_digit_display_24 (.value(display_driver_12_out_7), .dp(1'b0));
  Hex_Digit_Display hex_digit_display_25 (.value(display_driver_13_out_6), .dp(1'b0));
  Hex_Digit_Display hex_digit_display_26 (.value(display_driver_13_out_7), .dp(1'b0));
  adder adder_13 (.in1(adder_11_out), .in2(display_driver_13_register), .out(adder_13_out));
  Display_Driver display_driver_13 (
    .data(display_driver_11_data_2), .pos(display_driver_11_pos_2), .addr(display_driver_11_addr_2),
    .clk(display_driver_11_clk_2), .dir(display_driver_11_dir_2), .out_6(display_driver_13_out_6),
    .out_7(display_driver_13_out_7), .register(display_driver_13_register),
    .data_2(display_driver_13_data_2), .pos_2(display_driver_13_pos_2), .addr_2(display_driver_13_addr_2),
    .clk_2(display_driver_13_clk_2), .dir_2(display_driver_13_dir_2), .pos_3(display_driver_13_pos_3),
    .isEmpty(pull_resistor_1_node));
  button button_11 (
    .addr_2(button_11_addr_2), .pos(display_driver_13_pos_3), .button(button_12_out),
    .trigger(button_2_trigger));  // open: addr
  Button button_12 (.out(button_12_out));
  inc4 inc4_1 (.in(pos), .out(inc4_1_out));
  Pull_Resistor pull_resistor_2 (.node(display_driver_2_isempty));
  Hex_Digit_Display hex_digit_display_27 (.value(display_driver_14_out_6));  // open: dp
  Hex_Digit_Display hex_digit_display_28 (.value(display_driver_14_out_7));  // open: dp
  adder adder_14 (.in1(adder_13_out), .in2(display_driver_14_register), .out(adder_14_out));
  Display_Driver display_driver_14 (
    .data(display_driver_13_data_2), .pos(display_driver_13_pos_2), .addr(display_driver_13_addr_2),
    .clk(display_driver_13_clk_2), .dir(display_driver_13_dir_2), .out_6(display_driver_14_out_6),
    .out_7(display_driver_14_out_7), .register(display_driver_14_register),
    .data_2(display_driver_14_data_2), .pos_2(pos), .addr_2(display_driver_14_addr_2),
    .clk_2(display_driver_14_clk_2), .dir_2(display_driver_14_dir_2));  // open: pos_3, isEmpty
  WLD wld_1 (
    .p1(botScore), .end1(display_driver_2_isempty), .end2(pull_resistor_1_node), .p2(adder_14_out));  // open: p1win, p2win, GameOver
endmodule

module adder (
  input  [7:0] in1,
  input  [7:0] in2,
  output [7:0] out
);

  Adder adder_1 (.a(in1), .b(in2), .out(out), .cin(1'b0));  // open: cout
endmodule

module WLD (
  input  [7:0] p1,
  input  end1,
  input  end2,
  input  [7:0] p2,
  output p1win,
  output p2win,
  output GameOver
);

  wire comparator_1_eq, comparator_1_gt, comparator_1_lt, or_1_out, or_2_out;

  nand nand_1 (GameOver, end1, end2);
  Comparator comparator_1 (.a(p1), .b(p2), .gt(comparator_1_gt), .eq(comparator_1_eq), .lt(comparator_1_lt));
  and and_1 (p1win, or_1_out, GameOver);
  or or_1 (or_1_out, comparator_1_gt, comparator_1_eq);
  or or_2 (or_2_out, comparator_1_eq, comparator_1_lt);
  and and_2 (p2win, or_2_out, GameOver);

  // Other names for the same wires on the sheet: over = GameOver
endmodule

module button (
  input  [3:0] pos,
  input  [3:0] addr,
  input  button,
  output [3:0] addr_2,
  output trigger
);

  assign addr = button ? pos : 4'bz;  // Controlled_Buffer controlled_buffer_1
  Transistor #(.\type ("n")) transistor_1 (.in(1'b0), .out(trigger), .gate(button));

  assign addr_2 = addr;
endmodule

module inc4 (
  input  [3:0] in,
  output [3:0] out
);

  Adder #(.width(4)) adder_1 (.a(in), .b(4'b0001), .out(out), .cin(1'b0));  // open: cout
endmodule
